# Fritzing sketch SmartHouseRemoteESP (saved by Fritzing 0.9.3b)
circuit board: 8.46667cm x 5.64444cm
perfboards: 1

parts:
  R1 = Resistor [tolerance=±5% resistance=220 package=THT]
  U1 = TLP621 [package=THT]
  R2 = Resistor [tolerance=±5% resistance=10k package=THT]
  S2 = Pushbutton [package="[THT]"]
  Q1 = NPN-Transistor [package="TO92 [THT]"]
  J1 = longpad pin header, 5 pins [form="long pad"]
  U2 = TLP621 [package=THT]
  R3 = Resistor [tolerance=±5% resistance=220 package=THT]
  R4 = Resistor [tolerance=±5% resistance=10k package=THT]
  Q2 = NPN-Transistor [package="TO92 [THT]"]
  S1 = Pushbutton [package="[THT]"]

nets:
  N1: R1.Pin_0, J1.pin5, R3.Pin_0
  N2: R1.Pin_1, U1.Pin_1
  N3: U1.Pin_2, Q1.C
  N4: U1.Pin_4, S1.Pin_3, S1.Pin_4
  N5: U1.Pin_3, S1.Pin_1, S1.Pin_2
  N6: R2.Pin_0, J1.pin4
  N7: R2.Pin_1, Q1.B
  N8: S2.Pin_1, S2.Pin_2, U2.Pin_3
  N9: S2.Pin_3, S2.Pin_4, U2.Pin_4
  N10: Q1.E, J1.pin1, Q2.E
  N11: J1.pin3, R4.Pin_0
  N12: U2.Pin_1, R3.Pin_1
  N13: U2.Pin_2, Q2.C
  N14: R4.Pin_1, Q2.B

// code stored in the sketch: SmartHomeRemote.ino

